// Logisim project RV32_IM.circ as structural Verilog: 2 circuits, main circuit main
module main (
);

  wire W_EN;
  wire [31:0] ADDR, DATA, INST;

  Clock clock_1 (.out(W_EN));
  CPU cpu_1 (.in_1(INST), .in_2(W_EN), .out_5(W_EN), .out_3(ADDR), .out_4(DATA));
  RAM #(.addrWidth(24), .dataWidth(32), .enables("line")) ram_1 (
    .addr(ADDR[23:0]), .we(W_EN), .clk(W_EN), .din(DATA), .dout(INST));
endmodule

module CPU (
  input  [31:0] in_1,
  input  in_2,
  output [31:0] out_3,
  output [31:0] out_4,
  output out_5
);

  wire B_beq, B_blt, B_bltu, B_TYPE, comparator_1_eq, comparator_2_eq, comparator_3_eq, comparator_4_eq,
       comparator_5_eq, comparator_6_eq, comparator_7_eq, comparator_8_eq, comparator_9_eq, comparator_10_eq,
       comparator_11_eq, comparator_12_eq, comparator_13_eq, comparator_14_eq, comparator_15_eq,
       comparator_16_eq, comparator_17_eq, comparator_18_eq, comparator_19_eq, comparator_20_eq,
       comparator_21_eq, comparator_22_eq, comparator_23_eq, comparator_24_eq, comparator_25_eq,
       comparator_26_eq, comparator_27_eq, comparator_28_eq, comparator_29_eq, comparator_30_eq,
       comparator_31_eq, comparator_32_eq, comparator_41_eq, comparator_42_eq, comparator_43_eq,
       comparator_44_eq, comparator_45_eq, comparator_46_eq, comparator_47_eq, comparator_48_eq,
       comparator_49_eq, comparator_50_eq, comparator_51_eq, comparator_52_eq, comparator_53_eq,
       comparator_54_eq, comparator_55_eq, comparator_56_eq, comparator_57_eq, comparator_58_eq, I_and,
       I_div, I_jalr, I_lb, I_lh, I_lw, I_mulh, I_or, I_rem, I_sll, I_slt, I_srl, I_TYPE_LOAD, I_TYPE_OTHER,
       I_xor, R_add, R_and, R_div, R_mul, R_mulh, R_or, R_rem, R_sll, R_slt, R_srl, R_sub, R_TYPE, S_sw,
       S_swge, S_TYPE, U_jal, U_TYPE_LOAD;
  wire [31:0] PC_1;

  Comparator #(.width(3)) comparator_1 (.a(in_1[14:12]), .b(3'b000), .eq(comparator_1_eq));  // open: gt, lt
  Comparator #(.width(7)) comparator_2 (.a(in_1[31:25]), .b({7{1'b0}}), .eq(comparator_2_eq));  // open: gt, lt
  Comparator #(.width(3)) comparator_3 (.a(in_1[14:12]), .b(3'b000), .eq(comparator_3_eq));  // open: gt, lt
  Comparator #(.width(7)) comparator_4 (.a(in_1[31:25]), .b(7'b0000001), .eq(comparator_4_eq));  // open: gt, lt
  Comparator #(.width(3)) comparator_5 (.a(in_1[14:12]), .b(3'b000), .eq(comparator_5_eq));  // open: gt, lt
  Comparator #(.width(7)) comparator_6 (.a(in_1[31:25]), .b(7'b0000010), .eq(comparator_6_eq));  // open: gt, lt
  Comparator #(.width(3)) comparator_7 (.a(in_1[14:12]), .b(3'b001), .eq(comparator_7_eq));  // open: gt, lt
  Comparator #(.width(7)) comparator_8 (.a(in_1[31:25]), .b({7{1'b0}}), .eq(comparator_8_eq));  // open: gt, lt
  Comparator #(.width(3)) comparator_9 (.a(in_1[14:12]), .b(3'b001), .eq(comparator_9_eq));  // open: gt, lt
  Comparator #(.width(7)) comparator_10 (.a(in_1[31:25]), .b(7'b0000001), .eq(comparator_10_eq));  // open: gt, lt
  Comparator #(.width(3)) comparator_11 (.a(in_1[14:12]), .b(3'b010), .eq(comparator_11_eq));  // open: gt, lt
  Comparator #(.width(7)) comparator_12 (.a(in_1[31:25]), .b({7{1'b0}}), .eq(comparator_12_eq));  // open: gt, lt
  and and_1 (R_add, R_TYPE, comparator_1_eq, comparator_2_eq);
  and and_2 (R_mul, R_TYPE, comparator_3_eq, comparator_4_eq);
  and and_3 (R_sub, R_TYPE, comparator_5_eq, comparator_6_eq);
  and and_4 (R_sll, R_TYPE, comparator_7_eq, comparator_8_eq);
  and and_5 (R_mulh, R_TYPE, comparator_9_eq, comparator_10_eq);
  and and_6 (R_slt, R_TYPE, comparator_11_eq, comparator_12_eq);
  Comparator #(.width(3)) comparator_13 (.a(in_1[14:12]), .b(3'b100), .eq(comparator_13_eq));  // open: gt, lt
  Comparator #(.width(7)) comparator_14 (.a(in_1[31:25]), .b({7{1'b0}}), .eq(comparator_14_eq));  // open: gt, lt
  Comparator #(.width(3)) comparator_15 (.a(in_1[14:12]), .b(3'b100), .eq(comparator_15_eq));  // open: gt, lt
  Comparator #(.width(7)) comparator_16 (.a(in_1[31:25]), .b(7'b0000001), .eq(comparator_16_eq));  // open: gt, lt
  Comparator #(.width(3)) comparator_17 (.a(in_1[14:12]), .b(3'b101), .eq(comparator_17_eq));  // open: gt, lt
  Comparator #(.width(7)) comparator_18 (.a(in_1[31:25]), .b({7{1'b0}}), .eq(comparator_18_eq));  // open: gt, lt
  Comparator #(.width(3)) comparator_19 (.a(in_1[14:12]), .b(3'b110), .eq(comparator_19_eq));  // open: gt, lt
  Comparator #(.width(7)) comparator_20 (.a(in_1[31:25]), .b({7{1'b0}}), .eq(comparator_20_eq));  // open: gt, lt
  Comparator #(.width(3)) comparator_21 (.a(in_1[14:12]), .b(3'b110), .eq(comparator_21_eq));  // open: gt, lt
  Comparator #(.width(7)) comparator_22 (.a(in_1[31:25]), .b(7'b0000001), .eq(comparator_22_eq));  // open: gt, lt
  Comparator #(.width(3)) comparator_23 (.a(in_1[14:12]), .b(3'b111), .eq(comparator_23_eq));  // open: gt, lt
  Comparator #(.width(7)) comparator_24 (.a(in_1[31:25]), .b({7{1'b0}}), .eq(comparator_24_eq));  // open: gt, lt
  and and_7 (R_add, R_TYPE, comparator_13_eq, comparator_14_eq);
  and and_8 (R_div, R_TYPE, comparator_15_eq, comparator_16_eq);
  and and_9 (R_srl, R_TYPE, comparator_17_eq, comparator_18_eq);
  and and_10 (R_or, R_TYPE, comparator_19_eq, comparator_20_eq);
  and and_11 (R_rem, R_TYPE, comparator_21_eq, comparator_22_eq);
  and and_12 (R_and, R_TYPE, comparator_23_eq, comparator_24_eq);
  Register #(.width(32)) PC (.D(PC_1), .en(in_2), .clk(in_2), .Q(out_3));  // open: clr
  Adder #(.width(32)) adder_1 (.a(out_3), .b(32'h1), .out(PC_1));  // open: cin, cout
  Comparator #(.width(3)) comparator_25 (.a(in_1[14:12]), .b(3'b000), .eq(comparator_25_eq));  // open: gt, lt
  Comparator #(.width(3)) comparator_26 (.a(in_1[14:12]), .b(3'b001), .eq(comparator_26_eq));  // open: gt, lt
  Comparator #(.width(3)) comparator_27 (.a(in_1[14:12]), .b(3'b010), .eq(comparator_27_eq));  // open: gt, lt
  Comparator #(.width(3)) comparator_28 (.a(in_1[14:12]), .b(3'b010), .eq(comparator_28_eq));  // open: gt, lt
  Comparator #(.width(3)) comparator_29 (.a(in_1[14:12]), .b(3'b111), .eq(comparator_29_eq));  // open: gt, lt
  Comparator #(.width(3)) comparator_30 (.a(in_1[14:12]), .b(3'b000), .eq(comparator_30_eq));  // open: gt, lt
  Comparator #(.width(3)) comparator_31 (.a(in_1[14:12]), .b(3'b100), .eq(comparator_31_eq));  // open: gt, lt
  Comparator #(.width(3)) comparator_32 (.a(in_1[14:12]), .b(3'b110), .eq(comparator_32_eq));  // open: gt, lt
  and and_13 (I_lb, I_TYPE_LOAD, comparator_25_eq);
  and and_14 (I_lh, I_TYPE_LOAD, comparator_26_eq);
  and and_15 (I_lw, I_TYPE_LOAD, comparator_27_eq);
  and and_16 (S_sw, S_TYPE, comparator_28_eq);
  and and_17 (S_swge, S_TYPE, comparator_29_eq);
  and and_18 (B_beq, B_TYPE, comparator_30_eq);
  and and_19 (B_blt, B_TYPE, comparator_31_eq);
  and and_20 (B_bltu, B_TYPE, comparator_32_eq);
  Comparator #(.width(7)) comparator_33 (.a(in_1[6:0]), .b(7'b0110011), .eq(R_TYPE));  // open: gt, lt
  Comparator #(.width(7)) comparator_34 (.a(in_1[6:0]), .b(7'b0000011), .eq(I_TYPE_LOAD));  // open: gt, lt
  Comparator #(.width(7)) comparator_35 (.a(in_1[6:0]), .b(7'b0010011), .eq(I_TYPE_OTHER));  // open: gt, lt
  Comparator #(.width(7)) comparator_36 (.a(in_1[6:0]), .b(7'b0100011), .eq(S_TYPE));  // open: gt, lt
  Comparator #(.width(7)) comparator_37 (.a(in_1[6:0]), .b(7'b1100011), .eq(B_TYPE));  // open: gt, lt
  Comparator #(.width(7)) comparator_38 (.a(in_1[6:0]), .b(7'b0110111), .eq(U_TYPE_LOAD));  // open: gt, lt
  Comparator #(.width(7)) comparator_39 (.a(in_1[6:0]), .b(7'b1100111), .eq(U_jal));  // open: gt, lt
  Comparator #(.width(7)) comparator_40 (.a(in_1[6:0]), .b(7'b1101111), .eq(I_jalr));  // open: gt, lt
  Comparator #(.width(3)) comparator_41 (.a(in_1[14:12]), .b(3'b001), .eq(comparator_41_eq));  // open: gt, lt
  Comparator #(.width(7)) comparator_42 (.a(in_1[31:25]), .b({7{1'b0}}), .eq(comparator_42_eq));  // open: gt, lt
  Comparator #(.width(3)) comparator_43 (.a(in_1[14:12]), .b(3'b001), .eq(comparator_43_eq));  // open: gt, lt
  Comparator #(.width(7)) comparator_44 (.a(in_1[31:25]), .b(7'b0000001), .eq(comparator_44_eq));  // open: gt, lt
  Comparator #(.width(3)) comparator_45 (.a(in_1[14:12]), .b(3'b010), .eq(comparator_45_eq));  // open: gt, lt
  Comparator #(.width(7)) comparator_46 (.a(in_1[31:25]), .b({7{1'b0}}), .eq(comparator_46_eq));  // open: gt, lt
  Comparator #(.width(3)) comparator_47 (.a(in_1[14:12]), .b(3'b100), .eq(comparator_47_eq));  // open: gt, lt
  Comparator #(.width(7)) comparator_48 (.a(in_1[31:25]), .b({7{1'b0}}), .eq(comparator_48_eq));  // open: gt, lt
  Comparator #(.width(3)) comparator_49 (.a(in_1[14:12]), .b(3'b100), .eq(comparator_49_eq));  // open: gt, lt
  Comparator #(.width(7)) comparator_50 (.a(in_1[31:25]), .b(7'b0000001), .eq(comparator_50_eq));  // open: gt, lt
  and and_21 (I_sll, I_TYPE_OTHER, comparator_41_eq, comparator_42_eq);
  and and_22 (I_mulh, I_TYPE_OTHER, comparator_43_eq, comparator_44_eq);
  and and_23 (I_slt, I_TYPE_OTHER, comparator_45_eq, comparator_46_eq);
  and and_24 (I_xor, I_TYPE_OTHER, comparator_47_eq, comparator_48_eq);
  and and_25 (I_div, I_TYPE_OTHER, comparator_49_eq, comparator_50_eq);
  Comparator #(.width(3)) comparator_51 (.a(in_1[14:12]), .b(3'b101), .eq(comparator_51_eq));  // open: gt, lt
  Comparator #(.width(7)) comparator_52 (.a(in_1[31:25]), .b({7{1'b0}}), .eq(comparator_52_eq));  // open: gt, lt
  Comparator #(.width(3)) comparator_53 (.a(in_1[14:12]), .b(3'b110), .eq(comparator_53_eq));  // open: gt, lt
  Comparator #(.width(7)) comparator_54 (.a(in_1[31:25]), .b({7{1'b0}}), .eq(comparator_54_eq));  // open: gt, lt
  Comparator #(.width(3)) comparator_55 (.a(in_1[14:12]), .b(3'b110), .eq(comparator_55_eq));  // open: gt, lt
  Comparator #(.width(7)) comparator_56 (.a(in_1[31:25]), .b(7'b0000001), .eq(comparator_56_eq));  // open: gt, lt
  Comparator #(.width(3)) comparator_57 (.a(in_1[14:12]), .b(3'b111), .eq(comparator_57_eq));  // open: gt, lt
  Comparator #(.width(7)) comparator_58 (.a(in_1[31:25]), .b({7{1'b0}}), .eq(comparator_58_eq));  // open: gt, lt
  and and_26 (I_srl, I_TYPE_OTHER, comparator_51_eq, comparator_52_eq);
  and and_27 (I_or, I_TYPE_OTHER, comparator_53_eq, comparator_54_eq);
  and and_28 (I_rem, I_TYPE_OTHER, comparator_55_eq, comparator_56_eq);
  and and_29 (I_and, I_TYPE_OTHER, comparator_57_eq, comparator_58_eq);

  // Other names for the same wires on the sheet: CLK = in_2; I_TYPE_JUMP = I_jalr; PC[31:0] = out_3;
  //   RAM_ADDR[31:0] = out_3; RAM_DATA[31:0] = out_4; OPCODE[6:0] = in_1[6:0]; RAM_INSTRUCTION[31:0] = in_1;
  //   IMM_11_B = in_1[7]; RD[4:0] = in_1[11:7]; IMM_4_1[3:0] = in_1[11:8]; FUNCT3[2:0] = in_1[14:12];
  //   IMM_19_12[7:0] = in_1[19:12]; IMM_31_12[19:0] = in_1[31:12]; RS1[4:0] = in_1[19:15];
  //   IMM_11_0[11:0] = in_1[31:20]; IMM_11_J = in_1[20]; RS2[4:0] = in_1[24:20]; IMM_10_1[8:0] = in_1[29:21];
  //   FUNCT7[6:0] = in_1[31:25]; IMM_10_5[5:0] = in_1[30:25]; IMM_11_5[5:0] = in_1[31:26]; IMM_20[1:0] = in_1[31:30];
  //   IMM_12 = in_1[31]; RAM_WRITE_EN = out_5; U_lui = U_jal; U_TYPE_JUMP = U_jal

  // Notes on the sheet:
  //   outputs
  //   R-Type
  //   I-Type
  //   U-Type
  //   S-Type
  //   B-Type
  //   J-Type
  //   IMM_4_0
  //   I/O
  //   FETCH
  //   DECODE
  //   INSTRUCTION DECODING
  //   inputs
endmodule
